// Logisim project cpu.circ as structural Verilog: 1 circuit, main circuit main
module main (
  input  [31:0] INSTRUCTION,
  input  CLOCK,
  output [31:0] PROGRAM_COUNTER,
  output [31:0] ra,
  output [31:0] sp,
  output [31:0] t0,
  output [31:0] t1,
  output [31:0] t2,
  output [31:0] s0,
  output [31:0] s1,
  output [31:0] a0,
  output [31:0] out_12
);

  wire a_sel, b_sel, branch_comp_1_breq, branch_comp_1_brlt, control_logic_1_brun, men_sel, pc_sel, reg_w_en;
  wire [1:0] wb_sel;
  wire [2:0] func3, imm_sel;
  wire [3:0] alu_sel;
  wire [6:0] func7;
  wire [24:0] inst_reg;
  wire [31:0] adder_1_out, adder_2_out, alu_res, bit_extender_1_out, bit_extender_2_out, DMEM_p5, mem_res,
       multiplexer_1_out, multiplexer_2_out, multiplexer_3_out, multiplexer_4_out, pc_reg, r1, r2, wb;

  control_logic control_logic_1 (
    .BSel(b_sel), .BrUn(control_logic_1_brun), .RegWEn(reg_w_en), .ImmSel(imm_sel), .ASel(a_sel),
    .PCSel(pc_sel), .BrLt(branch_comp_1_brlt), .BrEq(branch_comp_1_breq),
    .inst({func7, inst_reg[24:15], func3, inst_reg[11:0]}), .ALUSel(alu_sel), .MemRW(men_sel), .WBSel(wb_sel));
  Multiplexer #(.width(32), .enable("false")) multiplexer_1 (
    .in0(adder_1_out), .in1(alu_res), .out(multiplexer_1_out), .sel(pc_sel));
  Register #(.width(32)) PC (.D(multiplexer_1_out), .clk(CLOCK), .Q(PROGRAM_COUNTER));  // open: en, clr
  Multiplexer #(.width(32), .enable("false")) multiplexer_2 (
    .in0(INSTRUCTION), .in1(32'h13), .out(multiplexer_2_out), .sel(pc_sel));
  imm_gen imm_gen_1 (.ImmSel(imm_sel), .inst({func7, inst_reg[24:15], func3, inst_reg[11:0]}), .imm(out_12));
  Register #(.width(32)) u_inst_reg (
    .D(multiplexer_2_out), .clk(CLOCK), .Q({func7, inst_reg[24:15], func3, inst_reg[11:0]}));  // open: en, clr
  Register #(.width(32)) u_pc_reg (.D(PROGRAM_COUNTER), .clk(CLOCK), .Q(pc_reg));  // open: en, clr
  Adder #(.width(32)) adder_1 (.a(PROGRAM_COUNTER), .b(32'h4), .out(adder_1_out));  // open: cin, cout
  branch_comp branch_comp_1 (
    .BrEq(branch_comp_1_breq), .BrUn(control_logic_1_brun), .rs1(r1), .BrLt(branch_comp_1_brlt), .rs2(r2));
  regfile_main RegFile (
    .rs2(inst_reg[24:20]), .rd(inst_reg[11:7]), .Read_Data_1(r1), .Read_Data_2(r2), .ra(ra), .sp(sp),
    .t0(t0), .t1(t1), .t2(t2), .s0(s0), .s1(s1), .a0(a0), .rs1(inst_reg[19:15]), .Write_Data(wb),
    .RegWEn(reg_w_en), .clk(CLOCK));
  Multiplexer #(.width(32), .enable("false")) multiplexer_3 (
    .in0(r1), .in1(pc_reg), .out(multiplexer_3_out), .sel(a_sel));
  Multiplexer #(.width(32), .enable("false")) multiplexer_4 (
    .in0(r2), .in1(out_12), .out(multiplexer_4_out), .sel(b_sel));
  Adder #(.width(32)) adder_2 (.a(pc_reg), .b(32'h4), .out(adder_2_out));  // open: cin, cout
  alu Arithmetic_Logic_Unit (.Result(alu_res), .ALUSel(alu_sel), .A(multiplexer_3_out), .B(multiplexer_4_out));
  Multiplexer #(.select(2), .width(32), .enable("false")) multiplexer_5 (
    .in0(alu_res), .in1(mem_res), .in2(adder_2_out), .out(wb), .sel(wb_sel));  // open: in3
  // mem_main DMEM: pin names not known; wires that end beside it: alu_res, r2, CLOCK, men_sel, DMEM_p5, DMEM_p5[7:0]
  assign bit_extender_1_out = {{24{DMEM_p5[7]}}, DMEM_p5[7:0]};  // Bit_Extender bit_extender_1
  assign bit_extender_2_out = {{16{DMEM_p5[15]}}, DMEM_p5[15:0]};  // Bit_Extender bit_extender_2
  Multiplexer #(.select(2), .width(32), .enable("false")) multiplexer_6 (
    .in0(bit_extender_1_out), .in1(bit_extender_2_out), .in2(DMEM_p5), .out(mem_res), .sel(func3[1:0]));  // open: in3

  // Other names for the same wires on the sheet: clk = CLOCK; imm[31:0] = out_12; op[6:0] = inst_reg[6:0];
  //   rd_addr[4:0] = inst_reg[11:7]; inst_reg (some bits) = {func7, func3}; r1_addr[4:0] = inst_reg[19:15];
  //   r2_addr[4:0] = inst_reg[24:20]

  // Notes on the sheet:
  //   Output
  //   IMEM (do **NOT** move this)
  //   Inputs
  //   It is OK to move the PC, RegFile, ALU, MEM, Branch Comp, Imm Gen, and Control Logic to wherever is most convenient for you when constructing your CPU, and to delete this text
  //   Inputs/Outputs for testing. Do **NOT** move these.
endmodule
