// Logisim project imm_gen.circ as structural Verilog: 1 circuit, main circuit imm_gen
module imm_gen (
  input  [31:0] inst,
  input  [2:0] ImmSel,
  output [31:0] imm
);

  Multiplexer #(.select(3), .width(32), .enable("false")) multiplexer_1 (
    .in0({{21{inst[31]}}, inst[30:20]}), .out(imm), .sel(ImmSel));  // open: in1, in2, in3, in4, in5, in6, in7

  // Other names for the same wires on the sheet: imm_I[31:0] = {{21{inst[31]}}, inst[30:20]}

  // Notes on the sheet:
  //   INPUTS to your circuit
  //   DON'T CHANGE THE LOCATIONS OF THE INPUTS AND OUTPUTS!
  //   OUTPUT from your circuit
endmodule
